# Fritzing sketch tal (saved by Fritzing 0.9.2b)
circuit board: 8.46667cm x 5.64444cm
breadboards: 1
perfboards: 1

parts:
  Part1 = Audio FX Sound Board
  Part2 = Arduino Pro Mini v13
  U1 = LIPO-2000mAh [package=lipo-2000]
  NEOPIXEL1 = Neopixel Strip -- White (60/m)
  Part3 = ST2012 2.8W Class D Stereo Amplifier

nets:
  VIN: Part1.VIN, Part2.RAW, U1.+, NEOPIXEL1.+5V
  GND: Part1.GND, Part2.GND, U1.-, NEOPIXEL1.GND, Part3.R-, Part3.L-
  N1: Part1.TX, Part2.D5_PWM
  N2: Part1.RX, Part2.D6_PWM
  N3: Part1.UG, Part3.GND
  N4: Part1.R, Part3.R+
  N5: Part1.L, Part3.L+
  N6: Part1.RST, Part2.D4
  N7: Part2.D7, NEOPIXEL1.DI

custom parts:
  Audio FX Sound Board: The Adafruit Sound Board, the fastest way to add audio effects to a project!
  Neopixel Strip -- White (60/m): Neopixel Strip, White, 60 pixels per meter.
