# Fritzing sketch talpi (saved by Fritzing 0.9.2b)
breadboards: 1
perfboards: 1

parts:
  Part1 = ST2012 2.8W Class D Stereo Amplifier
  Raspberry_Pi1 = Raspberry Pi B+  # not connected
  Arduino1 = Arduino Pro Mini v13
  J1 = Cobbler Plus  # not connected

nets:
  GND: Part1.GND, Arduino1.GND

custom parts:
  Cobbler Plus: The Cobbler Plus is an add on prototyping board from Adafruit specifically designed for the Raspberry Pi B+ that can break out all those tasty power, GPIO, I2C and SPI pins from the 40-pin header onto a solderless breadboard. This set will make "cobbling together" prototypes with the Pi super easy. The Cobbler Plus can plug into any solderless breadboard.
