# Fritzing sketch vest (saved by Fritzing 0.9.2b)
breadboards: 1

parts:
  Part1 = Arduino Pro Mini v13
  NEOPIXEL1 = Neopixel Strip -- White (30/m)
  U1 = LIPO-1000mAh [package=lipo-1000]
  Mute = SPST Switch [package=switch-spdt_kit]
  R1 = Resistor [tolerance=±5% resistance=330k package=THT]
  C1 = Capacitor Polarized [package=cpol-radial-1000uf-63v]
  J1 = Piezo Speaker

nets:
  N1: Part1.RAW, NEOPIXEL1.+5V, U1.+, C1.+
  GND: Part1.GND, NEOPIXEL1.GND, U1.-, Mute.P, C1.-
  N2: Part1.D9_PWM, J1.pin2
  N3: Part1.D5_PWM, R1.Pin_0
  N4: NEOPIXEL1.Din, R1.Pin_1
  N5: Mute.S, J1.pin1

custom parts:
  Neopixel Strip -- White (30/m): These NeoPixel strips have 30 digitally-addressable pixel LEDs per meter and are very affordable and are only 12.5 mm wide, 10 mm if you remove the strip from the casing.
